// Logisim project TallerLogica-Combinatorioss.circ as structural Verilog: 15 circuits, main circuit sumador_simple
module sumador_simple (
  input  A,
  input  B,
  output S,
  output Cout
);

  and and_1 (Cout, A, B);
  xor xor_1 (S, A, B);
endmodule

module sumador_completo (
  input  Cin,
  input  A,
  input  B,
  output S,
  output Cout
);

  wire sumador_simple_1_cout, sumador_simple_1_s, sumador_simple_2_cout;

  sumador_simple sumador_simple_1 (.A(A), .B(B), .S(sumador_simple_1_s), .Cout(sumador_simple_1_cout));
  sumador_simple sumador_simple_2 (.A(Cin), .B(sumador_simple_1_s), .S(S), .Cout(sumador_simple_2_cout));
  or or_1 (Cout, sumador_simple_2_cout, sumador_simple_1_cout);
endmodule

module sumador_4 (
  input  Cin,
  input  [3:0] A,
  input  [3:0] B,
  output [3:0] S,
  output Cout
);

  wire sumador_completo_1_cout, sumador_completo_2_cout, sumador_completo_3_cout;

  sumador_completo sumador_completo_1 (.Cin(Cin), .A(A[0]), .B(B[0]), .S(S[0]), .Cout(sumador_completo_1_cout));
  sumador_completo sumador_completo_2 (
    .Cin(sumador_completo_1_cout), .A(A[1]), .B(B[1]), .S(S[1]), .Cout(sumador_completo_2_cout));
  sumador_completo sumador_completo_3 (
    .Cin(sumador_completo_2_cout), .A(A[2]), .B(B[2]), .S(S[2]), .Cout(sumador_completo_3_cout));
  sumador_completo sumador_completo_4 (.Cin(sumador_completo_3_cout), .A(A[3]), .B(B[3]), .S(S[3]), .Cout(Cout));
  Hex_Digit_Display hex_digit_display_1 (.value(S));  // open: dp
endmodule

module comparador_cero (
  input  [3:0] A,
  output Z
);

  wire or_1_out, or_2_out, or_3_out;

  or or_1 (or_1_out, A[0], A[1]);
  or or_2 (or_2_out, A[2], A[3]);
  or or_3 (or_3_out, or_1_out, or_2_out);
  not not_1 (Z, or_3_out);
endmodule

module sumador_flags (
  input  Cin,
  input  [3:0] A,
  input  [3:0] B,
  output [3:0] S,
  output C,
  output Z,
  output N,
  output V
);

  wire not_1_out, xor_1_out, xor_2_out;

  sumador_4 sumador_4_1 (.Cin(Cin), .A(A), .B(B), .S({N, S[2:0]}), .Cout(C));
  xor xor_1 (xor_1_out, A[3], B[3]);
  not not_1 (not_1_out, xor_1_out);
  xor xor_2 (xor_2_out, B[3], N);
  and and_1 (V, not_1_out, xor_2_out);
  Hex_Digit_Display hex_digit_display_1 (.value({N, S[2:0]}));  // open: dp
  comparador_cero comparador_cero_1 (.A({N, S[2:0]}), .Z(Z));

  assign S[3] = N;
endmodule

module incrementador_4 (
  input  [3:0] A,
  output [3:0] S
);

  sumador_4 sumador_4_1 (.Cin(1'b0), .A(4'b0001), .B(A), .S(S));  // open: Cout
  Hex_Digit_Display hex_digit_display_1 (.value(S));  // open: dp
endmodule

module inversor_4 (
  input  [3:0] A,
  input  INV,
  output [3:0] S
);

  xor xor_1 (S[0], A[0], INV);
  xor xor_2 (S[1], A[1], INV);
  xor xor_3 (S[2], A[2], INV);
  xor xor_4 (S[3], A[3], INV);
  Hex_Digit_Display hex_digit_display_1 (.value(S));  // open: dp
endmodule

module ALU (
  input  [3:0] A,
  input  [3:0] B,
  input  [1:0] OP,
  output Z,
  output N,
  output V,
  output C,
  output [3:0] S
);

  wire restador_flags_1_c, restador_flags_1_n, restador_flags_1_v, restador_flags_1_z, sumador_flags_1_c,
       sumador_flags_1_n, sumador_flags_1_v, sumador_flags_1_z;
  wire [3:0] and_4_1_s, demultiplexer_1_out0, demultiplexer_1_out1, demultiplexer_1_out2,
       demultiplexer_1_out3, demultiplexer_2_out0, demultiplexer_2_out1, demultiplexer_2_out2,
       demultiplexer_2_out3, or_4_1_s, restador_flags_1_s, sumador_flags_1_s;

  Demultiplexer #(.select(2), .width(4)) demultiplexer_1 (
    .out0(demultiplexer_1_out0), .out1(demultiplexer_1_out1), .out2(demultiplexer_1_out2),
    .out3(demultiplexer_1_out3), .in(B), .sel(OP));
  Demultiplexer #(.select(2), .width(4)) demultiplexer_2 (
    .out0(demultiplexer_2_out0), .out1(demultiplexer_2_out1), .out2(demultiplexer_2_out2),
    .out3(demultiplexer_2_out3), .in(A), .sel(OP));
  sumador_flags sumador_flags_1 (
    .Cin(1'b0), .A(demultiplexer_2_out0), .B(demultiplexer_1_out0), .S(sumador_flags_1_s),
    .C(sumador_flags_1_c), .Z(sumador_flags_1_z), .N(sumador_flags_1_n), .V(sumador_flags_1_v));
  restador_flags restador_flags_1 (
    .A(demultiplexer_2_out1), .B(demultiplexer_1_out1), .S(restador_flags_1_s), .C(restador_flags_1_c),
    .Z(restador_flags_1_z), .V(restador_flags_1_v), .N(restador_flags_1_n));
  AND_4 and_4_1 (.A(demultiplexer_2_out2), .B(demultiplexer_1_out2), .S(and_4_1_s));
  OR_4 or_4_1 (.A(demultiplexer_2_out3), .B(demultiplexer_1_out3), .S(or_4_1_s));
  Multiplexer #(.select(2), .width(4)) multiplexer_1 (
    .in0(sumador_flags_1_s), .in1(restador_flags_1_s), .in2(and_4_1_s), .in3(or_4_1_s), .out(S), .sel(OP));
  Multiplexer #(.select(2)) multiplexer_2 (
    .in0(sumador_flags_1_z), .in1(restador_flags_1_z), .in2(1'b0), .in3(1'b0), .out(Z), .sel(OP));
  or or_1 (N, sumador_flags_1_n, restador_flags_1_n);
  or or_2 (V, sumador_flags_1_v, restador_flags_1_v);
  or or_3 (C, sumador_flags_1_c, restador_flags_1_c);
  Hex_Digit_Display hex_digit_display_1 (.value(S));  // open: dp
endmodule

module verificador (
  output [3:0] out_1,
  output [3:0] out_2,
  output [1:0] out_3,
  output halt,
  output N,
  output Z,
  output V,
  output C,
  output [3:0] res
);

  wire clock_1_out;

  Clock clock_1 (.out(clock_1_out));
  Counter #(.max('h3ff), .width(10)) counter_1 (
    .clk(clock_1_out), .carry(halt), .Q({out_3, out_2, out_1}));  // open: clr, load, up, count, D
  ALU alu_1 (.A(out_1), .B(out_2), .OP(out_3), .Z(N), .N(Z), .V(V), .C(C), .S(res));
endmodule

module medio_restador_simple (
  input  in_1,
  input  in_2,
  output out_3,
  output out_4
);

  wire not_1_out;

  not not_1 (not_1_out, in_1);
  xor xor_1 (out_3, in_1, in_2);
  and and_1 (out_4, in_2, not_1_out);
endmodule

module resta_1bit (
  input  A,
  input  B,
  input  Bin,
  output Diff,
  output Bout
);

  wire medio_restador_simple_1_out_3, medio_restador_simple_1_out_4, medio_restador_simple_2_out_4;

  medio_restador_simple medio_restador_simple_1 (
    .in_1(A), .in_2(B), .out_3(medio_restador_simple_1_out_3), .out_4(medio_restador_simple_1_out_4));
  medio_restador_simple medio_restador_simple_2 (
    .in_1(medio_restador_simple_1_out_3), .in_2(Bin), .out_3(Diff), .out_4(medio_restador_simple_2_out_4));
  or or_1 (Bout, medio_restador_simple_2_out_4, medio_restador_simple_1_out_4);
endmodule

module restador_4 (
  input  [3:0] A,
  input  [3:0] B,
  output [3:0] S,
  output Borrow
);

  wire resta_1bit_1_bout, resta_1bit_2_bout, resta_1bit_3_bout;

  resta_1bit resta_1bit_1 (.A(A[0]), .B(B[0]), .Bin(1'b0), .Diff(S[0]), .Bout(resta_1bit_1_bout));
  resta_1bit resta_1bit_2 (.A(A[1]), .B(B[1]), .Bin(resta_1bit_1_bout), .Diff(S[1]), .Bout(resta_1bit_2_bout));
  resta_1bit resta_1bit_3 (.A(A[2]), .B(B[2]), .Bin(resta_1bit_2_bout), .Diff(S[2]), .Bout(resta_1bit_3_bout));
  resta_1bit resta_1bit_4 (.A(A[3]), .B(B[3]), .Bin(resta_1bit_3_bout), .Diff(S[3]), .Bout(Borrow));
endmodule

module AND_4 (
  input  [3:0] A,
  input  [3:0] B,
  output [3:0] S
);

  and and_1 (S[0], A[0], B[0]);
  and and_2 (S[1], A[1], B[1]);
  and and_3 (S[2], A[2], B[2]);
  and and_4 (S[3], A[3], B[3]);
endmodule

module OR_4 (
  input  [3:0] A,
  input  [3:0] B,
  output [3:0] S
);

  or or_1 (S[0], A[0], B[0]);
  or or_2 (S[1], A[1], B[1]);
  or or_3 (S[2], A[2], B[2]);
  or or_4 (S[3], A[3], B[3]);
endmodule

module restador_flags (
  input  [3:0] A,
  input  [3:0] B,
  output [3:0] S,
  output C,
  output Z,
  output V,
  output N
);

  wire not_1_out, xor_1_out, xor_2_out;

  xor xor_1 (xor_1_out, B[3], A[3]);
  not not_1 (not_1_out, xor_1_out);
  xor xor_2 (xor_2_out, A[3], N);
  restador_4 restador_4_1 (.A(A), .B(B), .S({N, S[2:0]}), .Borrow(C));
  and and_1 (V, not_1_out, xor_2_out);
  comparador_cero comparador_cero_1 (.A({N, S[2:0]}), .Z(Z));

  assign S[3] = N;
endmodule
